// Digital circuit Digital223.dig as structural Verilog
module Digital223 (
  input  A,
  input  B,
  input  C,
  output D,
  output E,
  output F
);

  wire and_1_out, and_2_out, and_3_out, and_4_out, and_6_out, and_7_out, and_8_out, not_1_out, not_2_out,
       not_3_out, or_1_out, or_3_out;

  and and_1 (and_1_out, A, B);
  or or_1 (or_1_out, A, C);
  and and_2 (and_2_out, B, A);
  and and_3 (and_3_out, A, C);
  and and_4 (and_4_out, B, C);
  and and_5 (D, and_1_out, C);
  or or_2 (E, or_1_out, B);
  and and_6 (and_6_out, not_1_out, and_2_out);
  not not_1 (not_1_out, C);
  and and_7 (and_7_out, not_2_out, and_3_out);
  not not_2 (not_2_out, B);
  and and_8 (and_8_out, not_3_out, and_4_out);
  not not_3 (not_3_out, A);
  or or_3 (or_3_out, and_7_out, and_8_out);
  or or_4 (F, and_6_out, or_3_out);
endmodule
