// Digital circuit Digital232.dig as structural Verilog
module Digital232 (
  input  A,
  input  B,
  input  C,
  input  D,
  input  E,
  output OR,
  output AND,
  output NOT
);

  wire nor_2_out, nor_3_out, nor_4_out;

  nor nor_1 (NOT, A, A);
  nor nor_2 (nor_2_out, B, B);
  nor nor_3 (nor_3_out, C, C);
  nor nor_4 (nor_4_out, D, E);
  nor nor_5 (AND, nor_2_out, nor_3_out);
  nor nor_6 (OR, nor_4_out, nor_4_out);
endmodule
