// Digital circuit Digital242.dig as structural Verilog
module Digital242 (
  input  A_0,
  input  A_1,
  input  A_2,
  input  A_3,
  input  B_0,
  input  B_1,
  input  B_2,
  input  B_3,
  output OUT
);

  wire xnor_1_out, xnor_2_out, xnor_3_out, xnor_4_out;

  xnor xnor_1 (xnor_1_out, A_3, B_3);
  xnor xnor_2 (xnor_2_out, A_2, B_2);
  xnor xnor_3 (xnor_3_out, A_1, B_1);
  xnor xnor_4 (xnor_4_out, A_0, B_0);
  and and_1 (OUT, xnor_1_out, xnor_2_out, xnor_3_out, xnor_4_out);
endmodule
