// Digital circuit PC_Control.dig as structural Verilog
module PC_Control (
  input  [3:0] Cond,
  input  FlagSet,
  input  Branch,
  input  CLK,
  input  [3:0] NZCV,
  output PcOff
);

  wire and_1_out, and_2_out, and_3_out, and_4_out, and_5_out, and_6_out, and_7_out, not_1_out, not_2_out,
       not_3_out, not_4_out, not_5_out, not_6_out, not_7_out, not_8_out, not_9_out, not_10_out, not_11_out,
       not_12_out, not_13_out, or_1_out, xnor_1_out, xor_1_out;
  wire [3:0] register_1_q;

  and and_1 (and_1_out, FlagSet, CLK);
  Register #(.Bits(4)) register_1 (.D(NZCV), .C(and_1_out), .en(1'b1), .Q(register_1_q));
  not not_1 (not_1_out, register_1_q[2]);
  not not_2 (not_2_out, Cond[1]);
  not not_3 (not_3_out, Cond[2]);
  not not_4 (not_4_out, Cond[3]);
  not not_5 (not_5_out, Cond[0]);
  not not_6 (not_6_out, Cond[1]);
  not not_7 (not_7_out, Cond[2]);
  not not_8 (not_8_out, Cond[3]);
  not not_9 (not_9_out, register_1_q[2]);
  and and_2 (and_2_out, not_1_out, Cond[0], not_2_out, not_3_out, not_4_out);
  and and_3 (and_3_out, register_1_q[2], not_5_out, not_6_out, not_7_out, not_8_out);
  xor xor_1 (xor_1_out, register_1_q[0], register_1_q[3]);
  xnor xnor_1 (xnor_1_out, register_1_q[3], register_1_q[0]);
  and and_4 (and_4_out, not_10_out, Cond[1], Cond[2], Cond[3]);
  not not_10 (not_10_out, Cond[0]);
  not not_11 (not_11_out, Cond[2]);
  and and_5 (and_5_out, xnor_1_out, not_9_out);
  and and_6 (and_6_out, xor_1_out, Cond[0], Cond[1], not_11_out, Cond[3]);
  not not_12 (not_12_out, Cond[0]);
  not not_13 (not_13_out, Cond[1]);
  and and_7 (and_7_out, and_5_out, not_12_out, not_13_out, Cond[2], Cond[3]);
  or or_1 (or_1_out, and_2_out, and_3_out, and_6_out, and_7_out, and_4_out);
  and and_8 (PcOff, or_1_out, Branch);

  // Notes on the sheet:
  //   n = 3. bit
  //   b.ne
  //   b.eq
  //   b.lt
  //   b.gt
endmodule
