// Digital circuit ctrl_inst_decode.dig as structural Verilog
// Control unit of our minimal single cycle processor.
module ctrl_inst_decode (
  input  [31:0] Inst,
  output [3:0] Cond,
  output FlagSet,
  output Branch,
  output RegSrc,
  output RegW,
  output [1:0] ImmType,
  output AluSrc,
  output [1:0] AluCtrl,
  output MemW,
  output Mem2Reg
);

  wire and_1_out, and_2_out, and_4_out, and_6_out, and_7_out, and_9_out, and_11_out, nand_1_out, nor_1_out,
       not_1_out, or_2_out;

  and and_1 (and_1_out, Inst[27], Inst[28]);
  not not_1 (not_1_out, Inst[31]);
  and and_2 (and_2_out, Inst[24], ~and_1_out);  // And
  and and_3 (AluCtrl[1], ~Inst[24], Inst[25]);  // And
  and and_4 (and_4_out, not_1_out, Inst[30]);
  and and_5 (MemW, and_1_out, ~Inst[22]);  // And
  or or_1 (ImmType[1], AluCtrl[1], Inst[26]);
  or or_2 (or_2_out, and_2_out, AluCtrl[1]);
  and and_6 (and_6_out, Inst[30], and_2_out);
  and and_7 (and_7_out, AluCtrl[1], Inst[29]);
  and and_8 (Mem2Reg, and_1_out, Inst[22]);
  and and_9 (and_9_out, Inst[30], and_2_out);
  and and_10 (Branch, Inst[26], and_4_out);
  not not_2 (RegSrc, MemW);
  nor nor_1 (nor_1_out, MemW, Inst[26]);
  or or_3 (ImmType[0], and_2_out, Inst[26]);
  and and_11 (and_11_out, or_2_out, Inst[27]);
  or or_4 (AluCtrl[0], and_6_out, and_7_out);
  and and_12 (FlagSet, and_9_out, Inst[29]);
  nand nand_1 (nand_1_out, Inst[0], Inst[1], Inst[2], Inst[3], Inst[4]);
  not not_3 (AluSrc, and_11_out);
  and and_13 (RegW, nor_1_out, nand_1_out);

  assign Cond = Inst[3:0];

  // Notes on the sheet:
  //   Inst: A64 instruction.
  //   Cond: Condition codes if B.COND.
  //   31 == 0
  //   30 == 1
  //   LDR, STR
  //   ADD, SUB
  //   AND, ORR
  //   B.COND
  //   26. BIT
  //   STR
  //   AND, ORR,
  //   B.COND
  //   ADD, ORR,
  //   SUB, AND
  //   SUB
  //   ORR
  //   LDR
  //   29. BIT
  //   Branch Bool
  //   Register: ADD,
  //   SUB, AND, ORR
  //   SUBS
  //   Reg ID
  //   not 31
endmodule

/* Test case ADD(S), SUB(S), AND(S), ORR:
Inst       RegSrc RegW ImmType AluSrc AluCtrl MemW Mem2Reg FlagSet
0xb27f0be0      x    1       2      1       3     0       0       0 # orr x0, xzr, #14
0xb24007e1      x    1       2      1       3     0       0       0 # orr x1, xzr, #3
0x8b010002      1    1       x      0       0     0       0       0 # add x2, x0, x1
0xcb020023      1    1       x      0       1     0       0       0 # sub x3, x1, x2
0x8a030044      1    1       x      0       2     0       0       0 # and x4, x2, x3
0x91001c00      x    1       1      1       0     0       0       0 # add x0, x0, #7
*/

/* Test case FlagSet, Branch, Cond:
Inst       RegSrc RegW ImmType AluSrc AluCtrl MemW Mem2Reg FlagSet Branch Cond
0xb24007e0      x     1       2      1       3     0       0	0	x	x	# orr x0, xzr, #3
0xf1000400      x     1       1      1       1     0       0	1	x	x	# subs x0, x0, #1
0x54ffffa1      x     x       3      1       0     0       0	0	1	1	# b.ne my_loop
*/

/* Test case LDR, STR:
Inst       RegSrc RegW ImmType AluSrc AluCtrl MemW Mem2Reg
0xf9400000      x     1       0      1       0     0       1 # ldr x0, [x0]
0xf9400001      x     1       0      1       0     0       1 # ldr x1, [x0]
0xf9400029      x     1       0      1       0     0       1 # ldr x9, [x1]

0xf9401131      x     1       0      1       0     0       1 # ldr x17, [x9, #32]

0xf9400002      x     1       0      1       0     0       1 # ldr x2, [x0]
0xf9400403      x     1       0      1       0     0       1 # ldr x3, [x0, #8]
0xf9400804      x     1       0      1       0     0       1 # ldr x4, [x0, #16]
0xf9400c05      x     1       0      1       0     0       1 # ldr x5, [x0, #24]

0xf9000022      0     0       0      1       0     1       x # str x2, [x1]
0xf9000423      0     0       0      1       0     1       x # str x3, [x1, #8]
0xf9000824      0     0       0      1       0     1       x # str x4, [x1, #16]
0xf9000c25      0     0       0      1       0     1       x # str x5, [x1, #24]
*/
