// Digital circuit dp_alu.dig as structural Verilog
// 64-bit Arithmetic and Logic Unit with NZCV flags.
module dp_alu (
  input  [1:0] Ctrl,
  input  [63:0] A,
  input  [63:0] B,
  output [63:0] Result,
  output [3:0] NZCV
);

  wire add_1_c_o, not_2_out, xnor_1_out, xor_1_out;
  wire [63:0] add_1_s, and_1_out, multiplexer_1_out, not_1_out, or_1_out;

  assign not_1_out = ~B;  // Not not_1, 64 bits wide
  Multiplexer #(.Bits(64)) multiplexer_1 (.sel(Ctrl[0]), .in_0(B), .in_1(not_1_out), .out(multiplexer_1_out));
  assign and_1_out = B & A;  // And and_1, 64 bits wide
  assign or_1_out = B | A;  // Or or_1, 64 bits wide
  not not_2 (not_2_out, Ctrl[1]);
  Add #(.Bits(64)) add_1 (.a(A), .b(multiplexer_1_out), .c_i(Ctrl[0]), .s(add_1_s), .c_o(add_1_c_o));
  xnor xnor_1 (xnor_1_out, A[63], B[63], Ctrl[0]);
  xor xor_1 (xor_1_out, add_1_s[63], A[63]);
  Multiplexer #(.Selector_Bits(2), .Bits(64)) multiplexer_2 (
    .sel(Ctrl), .in_0(add_1_s), .in_1(add_1_s), .in_2(and_1_out), .in_3(or_1_out),
    .out({NZCV[3], Result[62:0]}));
  and and_2 (NZCV[1], add_1_c_o, not_2_out);
  and and_3 (NZCV[0], not_2_out, xor_1_out, xnor_1_out);
  Comparator #(.Bits(64)) comparator_1 (.a({NZCV[3], Result[62:0]}), .b({64{1'b0}}), .eq(NZCV[2]));  // open: gt, lt

  assign Result[63] = NZCV[3];

  // Notes on the sheet:
  //   Ctrl: Control signal which selects the operation of the ALU.
  //   00: add
  //   01: sub
  //   10: and
  //   11: orr
  //   A: First input.
  //   B: Second input.
  //   Result: Result of the operation.
  //   NZCV: NZCV flags: Negative, Zero, Carry, oVerflow.
endmodule
