// Digital circuit dp_imm_decode.dig as structural Verilog
// Decodes the immediate of different 64-bit A64 instructions.
module dp_imm_decode (
  input  [1:0] \type ,
  input  [18:0] imm,
  output [63:0] dec
);

  wire [18:0] barrelshifter_1_out;
  wire [63:0] bitextender_1_out, dp_imm_log_decode_1_dec;

  dp_imm_log_decode dp_imm_log_decode_1 (
    .N(imm[17]), .imms(imm[10:5]), .immr(imm[16:11]), .dec(dp_imm_log_decode_1_dec));
  BarrelShifter #(.Bits(19)) barrelshifter_1 (.in(imm), .shift(5'b00010), .out(barrelshifter_1_out));
  BitExtender #(.inputBits(19), .outputBits(64)) bitextender_1 (.in(barrelshifter_1_out), .out(bitextender_1_out));
  Multiplexer #(.Selector_Bits(2), .Bits(64)) multiplexer_1 (
    .sel(\type ), .in_0({{49{1'b0}}, imm[16:5], 3'b000}), .in_1({{52{1'b0}}, imm[16:5]}),
    .in_2(dp_imm_log_decode_1_dec), .in_3(bitextender_1_out), .out(dec));

  // Notes on the sheet:
  //   type: Type of the immediate which is decoded:
  //   00: Bits 5-16 are left-shifted by 3 and sign extended.
  //   01: Sign extended bits 5-16.
  //   10: Bits 5-16 are decoded assuming a logical immediate.
  //   11: Bits 0-18 are left-shifted by 2 and sign extended.
  //   imm: Bits 5 - 23 of the instruction.
  //   BIt 22 is only used for type 01 and 11.
  //   BIt 5-9 and 23 is only used for type 11.
  //   dec: Decoded immediate, resulting in 64-bit value.
endmodule
