// Digital circuit dp_imm_decode_part.dig as structural Verilog
// Decodes the immediate of different 64-bit A64 instructions.
module dp_imm_decode_part (
  input  [1:0] \type ,
  input  [12:0] imm,
  output [63:0] dec
);

  wire [63:0] dp_imm_log_decode_1_dec;

  dp_imm_log_decode dp_imm_log_decode_1 (.N(imm[12]), .imms(imm[5:0]), .immr(imm[11:6]), .dec(dp_imm_log_decode_1_dec));
  Multiplexer #(.Selector_Bits(2), .Bits(64)) multiplexer_1 (
    .sel(\type ), .in_0({{49{1'b0}}, imm[11:0], 3'b000}), .in_1({{52{1'b0}}, imm[11:0]}),
    .in_2(dp_imm_log_decode_1_dec), .in_3({64{1'b0}}), .out(dec));

  // Notes on the sheet:
  //   type: Type of the immediate which is decoded:
  //   00: Bits 5-16 are left-shifted by 3 and sign extended.
  //   01: Sign extended bits 5-16.
  //   10: Bits 5-16 are decoded assuming a logical immediate.
  //   11: ignored (zero is returned).
  //   imm: Bits 10 - 22 of the instruction.
  //   dec: Decoded immediate, resulting in 64-bit value.
endmodule
