// Digital circuit dp_imm_log_decode.dig as structural Verilog
// Decodes a logical immediate of an A64 instruction.
// These immediates are split into three parts: N (1 bits), imms (6bits) and immr (6 bits):
// Details:
// https://developer.arm.com/documentation/ddi0596/2021-12/Base-Instructions/AND--immediate---Bitwise-AND--immediate--
// https://dinfuehr.github.io/blog/encoding-of-immediate-values-on-aarch64/
// Note: This circuit is limited to 64 bits.
module dp_imm_log_decode (
  input  N,
  input  [5:0] imms,
  input  [5:0] immr,
  output [63:0] dec
);

  wire and_1_out, and_2_out, and_3_out, and_4_out, and_5_out, and_6_out, and_7_out, and_8_out, not_14_out;
  wire [1:0] add_1_s, barrelshifter_1_out, not_2_out;
  wire [2:0] add_2_s, or_1_out;
  wire [3:0] add_3_s, barrelshifter_2_out, not_3_out;
  wire [4:0] add_4_s;
  wire [5:0] add_5_s, not_1_out;
  wire [6:0] add_6_s;
  wire [7:0] barrelshifter_3_out, not_4_out;
  wire [7:6] not_8_out;
  wire [15:0] barrelshifter_4_out, not_5_out;
  wire [15:12] not_9_out;
  wire [31:0] barrelshifter_5_out, not_6_out;
  wire [31:24] not_10_out;
  wire [63:0] barrelshifter_6_out, multiplexer_1_out, not_7_out, not_13_out;
  wire [63:32] not_12_out;
  wire [63:48] not_11_out;

  assign not_1_out = ~imms;  // Not not_1, 6 bits wide
  assign not_2_out = ~2'b00;  // Not not_2, 2 bits wide
  Add #(.Bits(2)) add_1 (.a({1'b0, imms[0]}), .b(2'b01), .c_i(1'b0), .s(add_1_s));  // open: c_o
  assign not_3_out = ~4'b0000;  // Not not_3, 4 bits wide
  Add #(.Bits(3)) add_2 (.a({1'b0, imms[1:0]}), .b(3'b001), .c_i(1'b0), .s(add_2_s));  // open: c_o
  assign not_4_out = ~{8{1'b0}};  // Not not_4, 8 bits wide
  Add #(.Bits(4)) add_3 (.a({1'b0, imms[2:0]}), .b(4'b0001), .c_i(1'b0), .s(add_3_s));  // open: c_o
  assign not_5_out = ~{16{1'b0}};  // Not not_5, 16 bits wide
  Add #(.Bits(5)) add_4 (.a({1'b0, imms[3:0]}), .b(5'b00001), .c_i(1'b0), .s(add_4_s));  // open: c_o
  assign not_6_out = ~{32{1'b0}};  // Not not_6, 32 bits wide
  Add #(.Bits(6)) add_5 (.a({1'b0, imms[4:0]}), .b(6'b000001), .c_i(1'b0), .s(add_5_s));  // open: c_o
  assign not_7_out = ~{64{1'b0}};  // Not not_7, 64 bits wide
  Add #(.Bits(7)) add_6 (.a({1'b0, imms}), .b(7'b0000001), .c_i(1'b0), .s(add_6_s));  // open: c_o
  BarrelShifter #(.Bits(2)) barrelshifter_1 (.in(not_2_out), .shift(add_1_s), .out(barrelshifter_1_out));
  BarrelShifter #(.Bits(4)) barrelshifter_2 (.in(not_3_out), .shift(add_2_s), .out(barrelshifter_2_out));
  BarrelShifter #(.Bits(8)) barrelshifter_3 (.in(not_4_out), .shift(add_3_s), .out(barrelshifter_3_out));
  BarrelShifter #(.Bits(16)) barrelshifter_4 (.in(not_5_out), .shift(add_4_s), .out(barrelshifter_4_out));
  BarrelShifter #(.Bits(32)) barrelshifter_5 (.in(not_6_out), .shift(add_5_s), .out(barrelshifter_5_out));
  BarrelShifter #(.Bits(64)) barrelshifter_6 (.in(not_7_out), .shift(add_6_s), .out(barrelshifter_6_out));
  and and_1 (and_1_out, imms[4], imms[5]);
  and and_2 (and_2_out, imms[3], and_1_out);
  assign not_8_out = ~barrelshifter_1_out;  // Not not_8, 2 bits wide
  assign not_9_out = ~barrelshifter_2_out;  // Not not_9, 4 bits wide
  assign not_10_out = ~barrelshifter_3_out;  // Not not_10, 8 bits wide
  assign not_11_out = ~barrelshifter_4_out;  // Not not_11, 16 bits wide
  assign not_12_out = ~barrelshifter_5_out;  // Not not_12, 32 bits wide
  assign not_13_out = ~barrelshifter_6_out;  // Not not_13, 64 bits wide
  and and_3 (and_3_out, imms[2], and_2_out);
  not not_14 (not_14_out, N);
  and and_4 (and_4_out, and_3_out, not_1_out[1], not_14_out);
  and and_5 (and_5_out, and_2_out, not_1_out[2], not_14_out);
  and and_6 (and_6_out, and_1_out, not_1_out[3], not_14_out);
  and and_7 (and_7_out, imms[5], not_1_out[4], not_14_out);
  and and_8 (and_8_out, not_1_out[5], not_14_out);
  or or_1 (or_1_out[0], and_5_out, and_7_out, N);
  or or_2 (or_1_out[1], and_6_out, and_7_out);
  or or_3 (or_1_out[2], and_8_out, N);
  Multiplexer #(.Selector_Bits(3), .Bits(64)) multiplexer_1 (
    .sel(or_1_out),
    .in_0({not_8_out, not_8_out, not_8_out, not_8_out, not_8_out, not_8_out, not_8_out, not_8_out, not_8_out, not_8_out, not_8_out, not_8_out, not_8_out, not_8_out, not_8_out, not_8_out, not_8_out, not_8_out, not_8_out, not_8_out, not_8_out, not_8_out, not_8_out, not_8_out, not_8_out, not_8_out, not_8_out, not_8_out, not_8_out, not_8_out, not_8_out, not_8_out}),
    .in_1({not_9_out, not_9_out, not_9_out, not_9_out, not_9_out, not_9_out, not_9_out, not_9_out, not_9_out, not_9_out, not_9_out, not_9_out, not_9_out, not_9_out, not_9_out, not_9_out}),
    .in_2({not_10_out, not_10_out, not_10_out, not_10_out, not_10_out, not_10_out, not_10_out, not_10_out}),
    .in_3({not_11_out, not_11_out, not_11_out, not_11_out}), .in_4({not_12_out, not_12_out}),
    .in_5(not_13_out), .in_6({64{1'b0}}), .in_7({64{1'b0}}), .out(multiplexer_1_out));
  BarrelShifter #(.Bits(64), .barrelShifterMode("rotate"), .direction("right")) barrelshifter_7 (
    .in(multiplexer_1_out), .shift({1'b0, immr}), .out(dec));

  // Notes on the sheet:
  //   N: N bit of logical instructions.
  //   imms: imms bits of logical instructions.
  //   dec: Decoded 64-bit immediate.
  //   immr: immr bits of logical instructions.
  //   leading ones
  //   in imms
  //   2-bit elements
  //   4-bit elements
  //   8-bit elements
  //   16-bit elements
  //   32-bit elements
  //   64-bit elements
  //   element sizes
  //   as one-hot
  //   element sizes
  //   as binary
endmodule
