// Digital circuit part_0_ldr.dig as structural Verilog
// Datapath of a 64-bit single cycle processor supporting only LDR (immediate).
module part_0_ldr (
  input  CLK
);

  wire [14:3] I_Mem_d_2;
  wire [31:0] I_Mem_d;
  wire [63:0] add_1_s, add_2_s, D_Mem_d, PC_q, Reg_File_da;

  // Probe on CLK
  // Probe on add_1_s
  Register #(.Bits(64), .isProgramCounter("true")) PC (.D(add_1_s), .C(CLK), .en(1'b1), .Q(PC_q));
  // Probe on PC_q
  Add #(.Bits(64)) add_1 (.a(PC_q), .b(64'h4), .c_i(1'b0), .s(add_1_s));  // open: c_o
  ROM #(.AddrBits(8), .Bits(32)) I_Mem (.A(PC_q[9:2]), .sel(1'b1), .D({I_Mem_d[31:22], I_Mem_d_2, I_Mem_d[9:0]}));
  // Probe on {I_Mem_d[31:22], I_Mem_d_2, I_Mem_d[9:0]}
  RegisterFile #(.AddrBits(5), .Bits(64)) Reg_File (
    .Din(D_Mem_d), .we(1'b1), .Rw(I_Mem_d[4:0]), .C(CLK), .Ra(I_Mem_d[9:5]), .Rb({5{1'b0}}), .Da(Reg_File_da));  // open: Db
  Add #(.Bits(64)) add_2 (.a(Reg_File_da), .b({{49{1'b0}}, I_Mem_d_2, 3'b000}), .c_i(1'b0), .s(add_2_s));  // open: c_o
  // Probe on {{49{1'b0}}, I_Mem_d_2, 3'b000}
  // Probe on D_Mem_d
  RAMDualPort #(.AddrBits(9), .Bits(64)) D_Mem (
    .A(add_2_s[11:3]), .Din({64{1'b0}}), .str(1'b0), .C(CLK), .ld(1'b1), .D(D_Mem_d));

  // Notes on the sheet:
  //   Clock
  //   PC Next
  //   PC Current
  //   contents of I_Mem (hex, n*v repeats v):
  //   f9400000,f9400001,f9400029,f9401131
  //   Inst
  //   Decoded Imm
  //   WB Value
endmodule
