// Digital circuit part_1_str.dig as structural Verilog
// Datapath of a 64-bit single cycle processor supporting:
// LDR (immediate),
// STR (immediate).
module part_1_str (
  input  CLK,
  input  RegW,
  input  MemW
);

  wire [14:3] I_Mem_d_2;
  wire [31:0] I_Mem_d;
  wire [63:0] add_1_s, add_2_s, D_Mem_d, PC_q, Reg_File_da, Reg_File_db;

  // Probe on CLK
  // Probe on add_1_s
  Register #(.Bits(64), .isProgramCounter("true")) PC (.D(add_1_s), .C(CLK), .en(1'b1), .Q(PC_q));
  // Probe on PC_q
  Add #(.Bits(64)) add_1 (.a(PC_q), .b(64'h4), .c_i(1'b0), .s(add_1_s));  // open: c_o
  ROM #(.AddrBits(8), .Bits(32)) I_Mem (.A(PC_q[9:2]), .sel(1'b1), .D({I_Mem_d[31:22], I_Mem_d_2, I_Mem_d[9:0]}));
  // Probe on {I_Mem_d[31:22], I_Mem_d_2, I_Mem_d[9:0]}
  RegisterFile #(.AddrBits(5), .Bits(64)) Reg_File (
    .Din(D_Mem_d), .we(RegW), .Rw(I_Mem_d[4:0]), .C(CLK), .Ra(I_Mem_d[9:5]), .Rb(I_Mem_d[4:0]),
    .Da(Reg_File_da), .Db(Reg_File_db));
  Add #(.Bits(64)) add_2 (.a(Reg_File_da), .b({{49{1'b0}}, I_Mem_d_2, 3'b000}), .c_i(1'b0), .s(add_2_s));  // open: c_o
  // Probe on {{49{1'b0}}, I_Mem_d_2, 3'b000}
  // Probe on D_Mem_d
  RAMDualPort #(.AddrBits(9), .Bits(64)) D_Mem (
    .A(add_2_s[11:3]), .Din(Reg_File_db), .str(MemW), .C(CLK), .ld(1'b1), .D(D_Mem_d));

  // Notes on the sheet:
  //   Clock
  //   PC Next
  //   PC Current
  //   contents of I_Mem (hex, n*v repeats v):
  //   f9400002,f9400403,f9400804,f9400c05,f9000022,f9000423,f9000824,f9000c25
  //   Inst
  //   Decoded Imm
  //   WB Value
endmodule
