// Digital circuit part_2_addi_subi.dig as structural Verilog
// Datapath of a 64-bit single cycle processor supporting:
// LDR (immediate),
// STR (immediate),
// ADD (immediate),
// SUB (immediate).
module part_2_addi_subi (
  input  CLK,
  input  RegW,
  input  MemW,
  input  [1:0] AluCtrl,
  input  Mem2Reg,
  input  ImmType,
  output [3:0] NZCV
);

  wire [11:0] I_Mem_d_2;
  wire [31:0] I_Mem_d;
  wire [63:0] add_1_s, D_Mem_d, dp_alu_1_result, multiplexer_1_out, multiplexer_2_out, PC_q, Reg_File_da,
       Reg_File_db;

  // Probe on CLK
  // Probe on add_1_s
  Register #(.Bits(64), .isProgramCounter("true")) PC (.D(add_1_s), .C(CLK), .en(1'b1), .Q(PC_q));
  // Probe on PC_q
  Add #(.Bits(64)) add_1 (.a(PC_q), .b(64'h4), .c_i(1'b0), .s(add_1_s));  // open: c_o
  ROM #(.AddrBits(8), .Bits(32)) I_Mem (.A(PC_q[9:2]), .sel(1'b1), .D({I_Mem_d[31:22], I_Mem_d_2, I_Mem_d[9:0]}));
  // Probe on {I_Mem_d[31:22], I_Mem_d_2, I_Mem_d[9:0]}
  RegisterFile #(.AddrBits(5), .Bits(64)) Reg_File (
    .Din(multiplexer_2_out), .we(RegW), .Rw(I_Mem_d[4:0]), .C(CLK), .Ra(I_Mem_d[9:5]), .Rb(I_Mem_d[4:0]),
    .Da(Reg_File_da), .Db(Reg_File_db));
  Multiplexer #(.Bits(64)) multiplexer_1 (
    .sel(ImmType), .in_0({{49{1'b0}}, I_Mem_d_2, 3'b000}), .in_1({{52{1'b0}}, I_Mem_d_2}),
    .out(multiplexer_1_out));
  dp_alu dp_alu_1 (.Ctrl(AluCtrl), .A(Reg_File_da), .B(multiplexer_1_out), .Result(dp_alu_1_result), .NZCV(NZCV));
  // Probe on multiplexer_1_out
  // Probe on multiplexer_2_out
  RAMDualPort #(.AddrBits(9), .Bits(64)) D_Mem (
    .A(dp_alu_1_result[11:3]), .Din(Reg_File_db), .str(MemW), .C(CLK), .ld(1'b1), .D(D_Mem_d));
  Multiplexer #(.Bits(64)) multiplexer_2 (
    .sel(Mem2Reg), .in_0(dp_alu_1_result), .in_1(D_Mem_d), .out(multiplexer_2_out));

  // Notes on the sheet:
  //   Clock
  //   PC Next
  //   PC Current
  //   contents of I_Mem (hex, n*v repeats v):
  //   f9400405,d10024a6,910038c7,f9000807
  //   Inst
  //   Decoded Imm
  //   WB Value
endmodule
