// Digital circuit part_4_shifted_register.dig as structural Verilog
// Datapath of a 64-bit single cycle processor supporting:
// LDR (immediate),
// STR (immediate),
// ADD (immediate),
// SUB (immediate),
// AND (immediate),
// ORR (immediate),
// ADD (shifted register),
// SUB (shifted register),
// AND (shifted register),
// ORR (shifted register).
module part_4_shifted_register (
  input  CLK
);

  wire ctrl_inst_decode_1_alusrc, ctrl_inst_decode_1_branch, ctrl_inst_decode_1_flagset,
       ctrl_inst_decode_1_mem2reg, ctrl_inst_decode_1_memw, ctrl_inst_decode_1_regsrc,
       ctrl_inst_decode_1_regw, pc_control_1_pcoff;
  wire [1:0] ctrl_inst_decode_1_aluctrl, ctrl_inst_decode_1_immtype;
  wire [3:0] ctrl_inst_decode_1_cond, dp_alu_1_nzcv;
  wire [4:0] multiplexer_2_out;
  wire [31:0] I_Mem_d;
  wire [63:0] add_1_s, D_Mem_d, dp_alu_1_result, dp_imm_decode_1_dec, multiplexer_1_out, multiplexer_3_out,
       multiplexer_4_out, PC_q, Reg_File_da, Reg_File_db;

  // Probe on add_1_s
  // Probe on CLK
  Register #(.Bits(64), .isProgramCounter("true")) PC (.D(add_1_s), .C(CLK), .en(1'b1), .Q(PC_q));
  Multiplexer #(.Bits(64)) multiplexer_1 (
    .sel(pc_control_1_pcoff), .in_0(64'h4), .in_1(dp_imm_decode_1_dec), .out(multiplexer_1_out));
  // Probe on PC_q
  Add #(.Bits(64)) add_1 (.a(PC_q), .b(multiplexer_1_out), .c_i(1'b0), .s(add_1_s));  // open: c_o
  ROM #(.AddrBits(8), .Bits(32)) I_Mem (.A(PC_q[9:2]), .sel(1'b1), .D(I_Mem_d));
  ctrl_inst_decode ctrl_inst_decode_1 (
    .Inst(I_Mem_d), .Cond(ctrl_inst_decode_1_cond), .FlagSet(ctrl_inst_decode_1_flagset),
    .Branch(ctrl_inst_decode_1_branch), .RegSrc(ctrl_inst_decode_1_regsrc), .RegW(ctrl_inst_decode_1_regw),
    .ImmType(ctrl_inst_decode_1_immtype), .AluSrc(ctrl_inst_decode_1_alusrc),
    .AluCtrl(ctrl_inst_decode_1_aluctrl), .MemW(ctrl_inst_decode_1_memw), .Mem2Reg(ctrl_inst_decode_1_mem2reg));
  // Probe on I_Mem_d
  Multiplexer #(.Bits(5)) multiplexer_2 (
    .sel(ctrl_inst_decode_1_regsrc), .in_0(I_Mem_d[4:0]), .in_1(I_Mem_d[20:16]), .out(multiplexer_2_out));
  RegisterFile #(.AddrBits(5), .Bits(64)) Reg_File (
    .Din(multiplexer_4_out), .we(ctrl_inst_decode_1_regw), .Rw(I_Mem_d[4:0]), .C(CLK), .Ra(I_Mem_d[9:5]),
    .Rb(multiplexer_2_out), .Da(Reg_File_da), .Db(Reg_File_db));
  dp_imm_decode dp_imm_decode_1 (.\type (ctrl_inst_decode_1_immtype), .imm(I_Mem_d[23:5]), .dec(dp_imm_decode_1_dec));
  Multiplexer #(.Bits(64)) multiplexer_3 (
    .sel(ctrl_inst_decode_1_alusrc), .in_0(Reg_File_db), .in_1(dp_imm_decode_1_dec), .out(multiplexer_3_out));
  dp_alu dp_alu_1 (
    .Ctrl(ctrl_inst_decode_1_aluctrl), .A(Reg_File_da), .B(multiplexer_3_out), .Result(dp_alu_1_result),
    .NZCV(dp_alu_1_nzcv));
  // Probe on dp_imm_decode_1_dec
  // Probe on multiplexer_4_out
  PC_Control pc_control_1 (
    .Cond(ctrl_inst_decode_1_cond), .FlagSet(ctrl_inst_decode_1_flagset), .Branch(ctrl_inst_decode_1_branch),
    .CLK(CLK), .NZCV(dp_alu_1_nzcv), .PcOff(pc_control_1_pcoff));
  RAMDualPort #(.AddrBits(9), .Bits(64)) D_Mem (
    .A(dp_alu_1_result[11:3]), .Din(Reg_File_db), .str(ctrl_inst_decode_1_memw), .C(CLK), .ld(1'b1),
    .D(D_Mem_d));
  Multiplexer #(.Bits(64)) multiplexer_4 (
    .sel(ctrl_inst_decode_1_mem2reg), .in_0(dp_alu_1_result), .in_1(D_Mem_d), .out(multiplexer_4_out));

  // Notes on the sheet:
  //   Clock
  //   PC Next
  //   PC Current
  //   contents of I_Mem (hex, n*v repeats v):
  //   b2400be0,8a1f0021,91000c02,91001023,cb030040
  //   Inst
  //   Decoded Imm
  //   WB Value
endmodule
